// Logisim project KITT.circ as structural Verilog: 1 circuit, main circuit KITT
module KITT (
  input  in_1,
  input  in_2,
  input  in_3,
  input  in_4,
  input  in_5,
  input  in_6
);

  wire clock_1_out, counter_1_carry;
  wire [3:0] counter_1_q;
  wire [7:0] rom_1_data;

  Clock clock_1 (.out(clock_1_out));
  LED led_1 (.in(rom_1_data[7]));
  LED led_2 (.in(rom_1_data[6]));
  Counter #(.width(4), .max('hd)) counter_1 (
    .clr(in_1), .load(in_2), .up(1'b1), .count(1'b1), .clk(clock_1_out), .D({in_6, in_5, in_4, in_3}),
    .carry(counter_1_carry), .Q(counter_1_q));
  LED led_3 (.in(rom_1_data[4]));
  LED led_4 (.in(rom_1_data[2]));
  LED led_5 (.in(rom_1_data[3]));
  LED led_6 (.in(rom_1_data[5]));
  LED led_7 (.in(rom_1_data[1]));
  LED led_8 (.in(rom_1_data[0]));
  ROM #(.addrWidth(4)) rom_1 (.addr(counter_1_q), .data(rom_1_data));

  // Notes on the sheet:
  //   GREG WOO, 260777364
  //   contents of rom_1 (hex, n*v repeats v):
  //   1 2 4 8 10 20 40 80 40 20 10 8 4 2
endmodule
